// Logisim project Bandit16.circ as structural Verilog: 15 circuits, main circuit main
module main (
);

  wire AI, aJMP, ALUOP1, ALUOP2, ALURO, and_1_out, and_2_out, and_3_out, and_4_out, and_5_out, and_6_out,
       and_7_out, and_8_out, and_9_out, AO, bank_switcher_1_ram_active, bank_switcher_1_rom_active, BI, BO,
       BSRA, BSRO, button_1_out, Carry, CE, CLK, CLK_out, CO, control_logic_1_nc, demultiplexer_1_out1,
       demultiplexer_1_out2, demultiplexer_1_out3, demultiplexer_1_out4, demultiplexer_1_out5,
       demultiplexer_1_out6, demultiplexer_1_out7, EndCMD, FI, FO, FSI, HLT, IIH, IIL, INTC,
       interupt_control_1_intjmp, IOH, IOI, IOL, IOLA, IOO, JC, JMP, JMPI, JN, JNI, JNZ, JO, JZ, KYB_CLR,
       KYB_Data_RDY, MI, Negative, nor_1_out, not_2_out, not_3_out, Not_CLK, or_1_out, or_2_out, Overflow,
       RAI, RAO, RegIn, RegOut, ROO, RST, SPAOut, SPDEC, SPDOut, SPIn, SPINC, XI, XO, YI, YO, Zero;
  wire [3:0] ALUOP;
  wire [6:0] keyboard_1_data;
  wire [7:0] flagsregister_1_flags_out;
  wire [7:7] pull_resistor_1_node;
  wire [15:0] Address_Bus, Data_Bus, Instruction_High, MAR_Out, PCAO;

  Clock u_CLK (.out(CLK_out));
  not not_1 (Not_CLK, CLK);
  assign CLK = not_2_out ? CLK_out : 1'bz;  // Controlled_Buffer controlled_buffer_1
  not not_2 (not_2_out, HLT);
  Button u_RST (.out(RST));
  Bank_Switcher bank_switcher_1 (
    .BSRO(BSRO), .BSRA(BSRA), .CLK(CLK), .RST(RST), .ROM_Active(bank_switcher_1_rom_active),
    .RAM_Active(bank_switcher_1_ram_active));
  and and_1 (and_1_out, ROO, bank_switcher_1_ram_active);
  Demultiplexer #(.select(4)) demultiplexer_1 (
    .out1(demultiplexer_1_out1), .out2(demultiplexer_1_out2), .out3(demultiplexer_1_out3),
    .out4(demultiplexer_1_out4), .out5(demultiplexer_1_out5), .out6(demultiplexer_1_out6),
    .out7(demultiplexer_1_out7), .in(1'b1), .sel(ALUOP));  // open: out0, out8, out9, out10, out11, out12, out13, out14, out15
  or or_1 (or_1_out, RAO, and_1_out);
  and and_2 (and_2_out, ROO, bank_switcher_1_rom_active);
  ReadOnlyMemory readonlymemory_1 (.MAR_Address_Bus(MAR_Out), .RO(and_2_out), .Data_Bus(Data_Bus));
  RandomAccessMemory randomaccessmemory_1 (
    .MAR_Address_Bus(MAR_Out), .RI(RAI), .RO(or_1_out), .CLK(CLK), .DataBus(Data_Bus), .Data_Bus(Data_Bus));
  Memory_Address_Register memory_address_register_1 (
    .CLK(CLK), .RST(RST), .Address_Bus(Address_Bus), .MI(MI), .MAR_Out(MAR_Out));
  Program_Counter program_counter_1 (
    .RST(RST), .Jmp(aJMP), .CE(CE), .CLK(CLK), .CounterIn(Data_Bus), .CO(CO), .Address_Bus_Out(Address_Bus),
    .PC_AO(PCAO));
  Registers registers_1 (
    .CLK(CLK), .RST(RST), .DataIn(Data_Bus), .AI(AI), .BI(BI), .XI(XI), .YI(YI), .AO(AO), .BO(BO), .XO(XO),
    .YO(YO), .DataOut(Data_Bus));
  ALU alu_1 (
    .ALUResultOut(ALURO), .ALUAdd(demultiplexer_1_out1), .ALUSub(demultiplexer_1_out2),
    .ALUAND(demultiplexer_1_out5), .ALUOR(demultiplexer_1_out6), .ALUXOR(demultiplexer_1_out7),
    .ALUSL(demultiplexer_1_out3), .ALUSR(demultiplexer_1_out4), .Data_Bus(Data_Bus), .ALUOP1(ALUOP1),
    .CLK(CLK), .RST(RST), .ALUOP2(ALUOP2), .Overflow(Overflow), .Zero(Zero), .ALUOUT(Data_Bus),
    .Carry(Carry), .Negative(Negative));
  InstructionRegister instructionregister_1 (
    .CLK(CLK), .RST(RST), .DataIn(Data_Bus), .IIH(IIH), .IOH(IOH), .IOLA(IOLA), .IIL(IIL), .IOL(IOL),
    .IOH_Permanent(Instruction_High), .DataOut(Data_Bus), .IOL_Address(Address_Bus));
  FlagsRegister flagsregister_1 (
    .FI(FI), .CLK(CLK), .RST(RST), .Zero_Flag_In(Zero), .Carry_Flag_In(Carry),
    .Input_Ready_Flag_In(KYB_Data_RDY), .Negative_Flag_In(Negative), .Overflow_Flag_In(Overflow),
    .Data_Bus(Data_Bus), .FSI(FSI),
    .Flags_Out({{3{flagsregister_1_flags_out[7]}}, flagsregister_1_flags_out[4:0]}));
  Pull_Resistor pull_resistor_1 (.node(pull_resistor_1_node[7]));
  Pull_Resistor pull_resistor_2 (.node(flagsregister_1_flags_out[7]));
  assign Data_Bus = FO ? {{8{pull_resistor_1_node[7]}}, {3{flagsregister_1_flags_out[7]}}, flagsregister_1_flags_out[4:0]} : 16'bz;  // Controlled_Buffer controlled_buffer_2
  not not_3 (not_3_out, flagsregister_1_flags_out[0]);
  and and_3 (and_3_out, not_3_out, JNZ);
  and and_4 (and_4_out, JZ, flagsregister_1_flags_out[0]);
  and and_5 (and_5_out, flagsregister_1_flags_out[1], JC);
  and and_6 (and_6_out, flagsregister_1_flags_out[3], JN);
  and and_7 (and_7_out, JO, flagsregister_1_flags_out[4]);
  Pull_Resistor pull_resistor_3 (.node(Address_Bus));
  Pull_Resistor pull_resistor_4 (.node(Data_Bus));
  DisplayTTY displaytty_1 (.Address_Bus(Address_Bus), .Data_Bus(Data_Bus), .IOO(IOO), .CLK(CLK));
  or or_2 (or_2_out, and_3_out, and_4_out, and_5_out, JMP, and_8_out);
  Hex_Digit_Display hex_digit_display_1 (.value(Address_Bus[15:12]));  // open: dp
  Hex_Digit_Display hex_digit_display_2 (.value(Address_Bus[11:8]));  // open: dp
  Hex_Digit_Display hex_digit_display_3 (.value(Data_Bus[15:12]));  // open: dp
  Hex_Digit_Display hex_digit_display_4 (.value(Data_Bus[11:8]));  // open: dp
  Output_Display output_display_1 (.Data_Bus(Data_Bus), .CLK(CLK), .RST(RST), .Address_Bus(Address_Bus), .IOO(IOO));
  nor nor_1 (nor_1_out, Address_Bus[1], Address_Bus[2], Address_Bus[4], Address_Bus[5], Address_Bus[6], Address_Bus[7], Address_Bus[8], Address_Bus[9], Address_Bus[10], Address_Bus[11], Address_Bus[12], Address_Bus[13], Address_Bus[14], Address_Bus[15], Address_Bus[0]);
  and and_8 (and_8_out, JNI, flagsregister_1_flags_out[2]);
  Button button_1 (.out(button_1_out));
  Hex_Digit_Display hex_digit_display_5 (.value(Address_Bus[7:4]));  // open: dp
  Hex_Digit_Display hex_digit_display_6 (.value(Data_Bus[7:4]));  // open: dp
  and and_9 (and_9_out, Address_Bus[3], nor_1_out, IOI);
  or or_3 (aJMP, BSRA, or_2_out, and_6_out, and_7_out, interupt_control_1_intjmp, BSRO);
  Hex_Digit_Display hex_digit_display_7 (.value(Address_Bus[3:0]));  // open: dp
  Hex_Digit_Display hex_digit_display_8 (.value(Data_Bus[3:0]));  // open: dp
  Keyboard keyboard_1 (.clk(CLK), .re(and_9_out), .clr(KYB_CLR), .avail(KYB_Data_RDY), .data(keyboard_1_data));
  Interupt_Control interupt_control_1 (
    .INT_Trig(button_1_out), .CLK(CLK), .RST(RST), .INT_RET(JMPI), .INTC(INTC), .PCAO(PCAO),
    .INTJMP(interupt_control_1_intjmp), .Data_Bus(Data_Bus));
  assign Data_Bus[6:0] = IOI ? keyboard_1_data : 7'bz;  // Controlled_Buffer controlled_buffer_3
  Stack_Pointer stack_pointer_1 (
    .SPINC(SPINC), .SPDEC(SPDEC), .Data_Bus_In(Data_Bus), .SPIn(SPIn), .SPAOut(SPAOut), .CLK(CLK), .RST(RST),
    .SPDOut(SPDOut), .Address_Bus_Out(Address_Bus), .Data_Bus_Out(Data_Bus));
  Control_Logic control_logic_1 (
    .Instruction(Instruction_High), .CLK(Not_CLK), .JN(JN), .JO(JO), .FO(FO), .FSI(FSI), .INTC(INTC),
    .JMPI(JMPI), .BSRO(BSRO), .BSRA(BSRA), .JMP(JMP), .JC(JC), .JZ(JZ), .JNZ(JNZ), .ALURO(ALURO),
    .EndCMD(EndCMD), .IOLA(IOLA), .FI(FI), .ALUOP1(ALUOP1), .ALUOP2(ALUOP2), .JNI(JNI), .SPIn(SPIn),
    .SPDOut(SPDOut), .SPAOut(SPAOut), .SPINC(SPINC), .SPDEC(SPDEC), .CE(CE), .CO(CO), .MI(MI), .RAO(RAO),
    .RAI(RAI), .ROO(ROO), .NC(control_logic_1_nc), .HLT(HLT), .RegOut(RegOut), .RegIn(RegIn), .IIL(IIL),
    .IIH(IIH), .IOL(IOL), .IOH(IOH), .IOO(IOO), .IOI(IOI), .ALUOP(ALUOP), .AO(AO), .BO(BO), .XO(XO), .YO(YO),
    .AI(AI), .BI(BI), .XI(XI), .YI(YI));
  Pull_Resistor pull_resistor_5 (.node(AO));
  Pull_Resistor pull_resistor_6 (.node(BO));
  Pull_Resistor pull_resistor_7 (.node(XO));
  Pull_Resistor pull_resistor_8 (.node(YO));
  Pull_Resistor pull_resistor_9 (.node(AI));
  Pull_Resistor pull_resistor_10 (.node(BI));
  Pull_Resistor pull_resistor_11 (.node(XI));
  Pull_Resistor pull_resistor_12 (.node(YI));
  Pull_Resistor pull_resistor_13 (.node(CE));
  Pull_Resistor pull_resistor_14 (.node(CO));
  Pull_Resistor pull_resistor_15 (.node(MI));
  Pull_Resistor pull_resistor_16 (.node(RAO));
  Pull_Resistor pull_resistor_17 (.node(RAI));
  Pull_Resistor pull_resistor_18 (.node(ROO));
  Pull_Resistor pull_resistor_19 (.node(HLT));
  Pull_Resistor pull_resistor_20 (.node(RegOut));
  Pull_Resistor pull_resistor_21 (.node(RegIn));
  Pull_Resistor pull_resistor_22 (.node(IIL));
  Pull_Resistor pull_resistor_23 (.node(IIH));
  Pull_Resistor pull_resistor_24 (.node(IOL));
  Pull_Resistor pull_resistor_25 (.node(IOH));
  Pull_Resistor pull_resistor_26 (.node(FI));
  Pull_Resistor pull_resistor_27 (.node(JC));
  Pull_Resistor pull_resistor_28 (.node(JZ));
  Pull_Resistor pull_resistor_29 (.node(JNZ));
  Pull_Resistor pull_resistor_30 (.node(ALURO));
  Pull_Resistor pull_resistor_31 (.node(IOO));
  Pull_Resistor pull_resistor_32 (.node(IOI));
  Pull_Resistor pull_resistor_33 (.node(ALUOP1));
  Pull_Resistor pull_resistor_34 (.node(ALUOP2));
  Pull_Resistor pull_resistor_35 (.node(JNI));
  Pull_Resistor pull_resistor_36 (.node(SPIn));
  Pull_Resistor pull_resistor_37 (.node(SPDOut));
  Pull_Resistor pull_resistor_38 (.node(SPAOut));
  Pull_Resistor pull_resistor_39 (.node(SPINC));
  Pull_Resistor pull_resistor_40 (.node(SPDEC));
  Pull_Resistor pull_resistor_41 (.node(JN));
  Pull_Resistor pull_resistor_42 (.node(JO));
  Pull_Resistor pull_resistor_43 (.node(FO));
  Pull_Resistor pull_resistor_44 (.node(FSI));
  Pull_Resistor pull_resistor_45 (.node(INTC));
  Pull_Resistor pull_resistor_46 (.node(JMPI));
  Pull_Resistor pull_resistor_47 (.node(BSRO));
  Pull_Resistor pull_resistor_48 (.node(BSRA));

  // Notes on the sheet:
  //   Interupt
  //   Keyboard
endmodule

module Program_Counter (
  input  RST,
  input  Jmp,
  input  CE,
  input  CLK,
  input  [15:0] CounterIn,
  input  CO,
  output [15:0] Address_Bus_Out,
  output [15:0] PC_AO
);

  Counter #(.max('hffff), .width(16)) counter_1 (
    .clr(RST), .load(Jmp), .up(1'b1), .count(CE), .clk(CLK), .D(CounterIn), .Q(PC_AO));  // open: carry
  Hex_Digit_Display hex_digit_display_1 (.value(PC_AO[15:12]));  // open: dp
  Hex_Digit_Display hex_digit_display_2 (.value(PC_AO[11:8]));  // open: dp
  Hex_Digit_Display hex_digit_display_3 (.value(PC_AO[7:4]));  // open: dp
  Hex_Digit_Display hex_digit_display_4 (.value(PC_AO[3:0]));  // open: dp
  assign Address_Bus_Out = CO ? PC_AO : 16'bz;  // Controlled_Buffer controlled_buffer_1
  LED led_1 (.in(PC_AO[0]));
  LED led_2 (.in(PC_AO[1]));
  LED led_3 (.in(PC_AO[2]));
  LED led_4 (.in(PC_AO[3]));
  LED led_5 (.in(PC_AO[4]));
  LED led_6 (.in(PC_AO[5]));
  LED led_7 (.in(PC_AO[6]));
  LED led_8 (.in(PC_AO[7]));
  LED led_9 (.in(PC_AO[8]));
  LED led_10 (.in(PC_AO[9]));
  LED led_11 (.in(PC_AO[10]));
  LED led_12 (.in(PC_AO[11]));
  LED led_13 (.in(PC_AO[12]));
  LED led_14 (.in(PC_AO[13]));
  LED led_15 (.in(PC_AO[14]));
  LED led_16 (.in(PC_AO[15]));
endmodule

module Registers (
  input  CLK,
  input  RST,
  input  [15:0] DataIn,
  input  AI,
  input  AO,
  input  BI,
  input  BO,
  input  XI,
  input  XO,
  input  YI,
  input  YO,
  output [15:0] DataOut
);

  wire [3:0] register_1_q, register_1_q_2, register_1_q_3, register_1_q_4, register_2_q, register_2_q_2,
       register_3_q, register_3_q_2, register_4_q, register_4_q_2;
  wire [15:8] register_2_q_3, register_3_q_3, register_4_q_3;

  Hex_Digit_Display hex_digit_display_1 (.value(register_1_q_4));  // open: dp
  Hex_Digit_Display hex_digit_display_2 (.value(register_1_q_3));  // open: dp
  Register #(.width(16)) register_1 (
    .D(DataIn), .en(AI), .clk(CLK), .Q({register_1_q_4, register_1_q_3, register_1_q_2, register_1_q}),
    .clr(RST));
  Register #(.width(16)) register_2 (
    .D(DataIn), .en(BI), .clk(CLK), .Q({register_2_q_3, register_2_q_2, register_2_q}), .clr(RST));
  Register #(.width(16)) register_3 (
    .D(DataIn), .en(XI), .clk(CLK), .Q({register_3_q_3, register_3_q_2, register_3_q}), .clr(RST));
  Register #(.width(16)) register_4 (
    .D(DataIn), .en(YI), .clk(CLK), .Q({register_4_q_3, register_4_q_2, register_4_q}), .clr(RST));
  Hex_Digit_Display hex_digit_display_3 (.value(register_1_q_2));  // open: dp
  Hex_Digit_Display hex_digit_display_4 (.value(register_1_q));  // open: dp
  assign DataOut = AO ? {register_1_q_4, register_1_q_3, register_1_q_2, register_1_q} : 16'bz;  // Controlled_Buffer controlled_buffer_1
  assign DataOut = BO ? {register_2_q_3, register_2_q_2, register_2_q} : 16'bz;  // Controlled_Buffer controlled_buffer_2
  assign DataOut = XO ? {register_3_q_3, register_3_q_2, register_3_q} : 16'bz;  // Controlled_Buffer controlled_buffer_3
  assign DataOut = YO ? {register_4_q_3, register_4_q_2, register_4_q} : 16'bz;  // Controlled_Buffer controlled_buffer_4
  Hex_Digit_Display hex_digit_display_5 (.value(register_2_q_3[15:12]));  // open: dp
  Hex_Digit_Display hex_digit_display_6 (.value(register_3_q_3[15:12]));  // open: dp
  Hex_Digit_Display hex_digit_display_7 (.value(register_4_q_3[15:12]));  // open: dp
  Hex_Digit_Display hex_digit_display_8 (.value(register_2_q_2));  // open: dp
  Hex_Digit_Display hex_digit_display_9 (.value(register_2_q_3[11:8]));  // open: dp
  Hex_Digit_Display hex_digit_display_10 (.value(register_3_q_2));  // open: dp
  Hex_Digit_Display hex_digit_display_11 (.value(register_3_q_3[11:8]));  // open: dp
  Hex_Digit_Display hex_digit_display_12 (.value(register_4_q_2));  // open: dp
  Hex_Digit_Display hex_digit_display_13 (.value(register_4_q_3[11:8]));  // open: dp
  Hex_Digit_Display hex_digit_display_14 (.value(register_2_q));  // open: dp
  Hex_Digit_Display hex_digit_display_15 (.value(register_3_q));  // open: dp
  Hex_Digit_Display hex_digit_display_16 (.value(register_4_q));  // open: dp
endmodule

module RandomAccessMemory (
  input  [15:0] MAR_Address_Bus,
  input  RI,
  input  RO,
  input  CLK,
  input  [15:0] DataBus,
  output [15:0] Data_Bus
);

  wire [15:0] ram_1_data;

  RAM #(.addrWidth(16), .asyncread("true"), .dataWidth(16), .databus("bidir")) ram_1 (
    .addr(MAR_Address_Bus), .we(RI), .oe(RO), .clk(CLK), .data(ram_1_data));
  assign Data_Bus = RO ? ram_1_data : 16'bz;  // Controlled_Buffer controlled_buffer_1
  assign ram_1_data = RI ? DataBus : 16'bz;  // Controlled_Buffer controlled_buffer_2
endmodule

module ReadOnlyMemory (
  input  [15:0] MAR_Address_Bus,
  input  RO,
  output [15:0] Data_Bus
);

  wire [15:0] rom_1_data;

  ROM #(.addrWidth(16), .dataWidth(16)) rom_1 (.addr(MAR_Address_Bus), .data(rom_1_data));
  assign Data_Bus = RO ? rom_1_data : 16'bz;  // Controlled_Buffer controlled_buffer_1

  // Notes on the sheet:
  //   contents of rom_1 (hex, n*v repeats v):
  //   400 ffff 1300 0 400 0 400 42 b00 4 400 61 b00 4 400 6e b00 4 400 64 b00 4 400 69 b00 4 400 74 b00 4
  //   400 2d b00 4 400 31 b00 4 400 36 b00 4 400 20 b00 4 400 4f b00 4 400 53 b00 4 400 20 b00 4 400 36
  //   b00 4 400 34 b00 4 400 4b b00 4 400 a b00 4 400 53 b00 4 400 74 b00 4 400 61 b00 4 400 63 b00 4 400
  //   6b b00 4 400 20 b00 4 400 49 b00 4 400 6e b00 4 400 69 b00 4 400 74 b00 4 400 69 b00 4 400 61 b00 4
  //   400 6c b00 4 400 69 b00 4 400 73 b00 4 400 65 b00 4 400 64 b00 4 400 20 b00 4 400 61 b00 4 400 74
  //   b00 4 400 20 b00 4 400 30 b00 4 400 78 b00 4 400 46 b00 4 400 46 b00 4 400 46 b00 4 400 46 b00 4 400
  //   a b00 4 400 49 b00 4 400 53 b00 4 400 52 b00 4 400 20 b00 4 400 49 b00 4 400 6e b00 4 400 69 b00 4
  //   400 74 b00 4 400 69 b00 4 400 61 b00 4 400 6c b00 4 400 69 b00 4 400 73 b00 4 400 65 b00 4 400 64
  //   b00 4 400 20 b00 4 400 61 b00 4 400 74 b00 4 400 20 b00 4 400 30 b00 4 400 78 b00 4 400 46 b00 4 400
  //   45 b00 4 400 30 b00 4 400 30 b00 4 400 a b00 4 400 52 b00 4 400 45 b00 4 400 41 b00 4 400 44 b00 4
  //   400 59 b00 4 400 a b00 4 400 3e b00 4 600 3e8 680*0 400 a b00 4 400 54 b00 4 400 65 b00 4 400 73 b00
  //   4 400 74 b00 4 400 20 b00 4 400 31 b00 4 400 3a b00 4 400 20 b00 4 400 41 b00 4 400 64 b00 4 400 64
  //   b00 4 400 69 b00 4 400 74 b00 4 400 69 b00 4 400 6f b00 4 400 6e b00 4 400 20 b00 4 400 28 b00 4 400
  //   35 b00 4 400 20 b00 4 400 2b b00 4 400 20 b00 4 400 36 b00 4 400 29 b00 4 400 a b00 4 400 52 b00 4
  //   400 65 b00 4 400 73 b00 4 400 75 b00 4 400 6c b00 4 400 74 b00 4 400 20 b00 4 400 73 b00 4 400 68
  //   b00 4 400 6f b00 4 400 75 b00 4 400 6c b00 4 400 64 b00 4 400 20 b00 4 400 62 b00 4 400 65 b00 4 400
  //   20 b00 4 400 30 b00 4 400 78 b00 4 400 30 b00 4 400 30 b00 4 400 30 b00 4 400 62 b00 4 400 a b00 4
  //   400 43 b00 4 400 68 b00 4 400 65 b00 4 400 63 b00 4 400 6b b00 4 400 20 b00 4 400 74 b00 4 400 68
  //   b00 4 400 65 b00 4 400 20 b00 4 400 48 b00 4 400 65 b00 4 400 78 b00 4 400 20 b00 4 400 4f b00 4 400
  //   75 b00 4 400 74 b00 4 400 70 b00 4 400 75 b00 4 400 74 b00 4 400 20 b00 4 400 a b00 4 400 50 b00 4
  //   400 72 b00 4 400 65 b00 4 400 73 b00 4 400 73 b00 4 400 20 b00 4 400 45 b00 4 400 6e b00 4 400 74
  //   b00 4 400 65 b00 4 400 72 b00 4 400 20 b00 4 400 74 b00 4 400 6f b00 4 400 20 b00 4 400 43 b00 4 400
  //   6f b00 4 400 6e b00 4 400 74 b00 4 400 69 b00 4 400 6e b00 4 400 75 b00 4 400 65 b00 4 400 a b00 4
  //   400 5 401 6 1000 0 1104 0 512 0 b08 2 1900 0 a00 1a08 600 574 400 a b00 4 400 54 b00 4 400 65 b00 4
  //   400 73 b00 4 400 74 b00 4 400 20 b00 4 400 32 b00 4 400 3a b00 4 400 20 b00 4 400 53 b00 4 400 75
  //   b00 4 400 62 b00 4 400 74 b00 4 400 72 b00 4 400 61 b00 4 400 63 b00 4 400 74 b00 4 400 69 b00 4 400
  //   6f b00 4 400 6e b00 4 400 20 b00 4 400 28 b00 4 400 31 b00 4 400 30 b00 4 400 2d b00 4 400 36 b00 4
  //   400 29 b00 4 400 a b00 4 400 52 b00 4 400 65 b00 4 400 73 b00 4 400 75 b00 4 400 6c b00 4 400 74 b00
  //   4 400 20 b00 4 400 73 b00 4 400 68 b00 4 400 6f b00 4 400 75 b00 4 400 6c b00 4 400 64 b00 4 400 20
  //   b00 4 400 62 b00 4 400 65 b00 4 400 20 b00 4 400 30 b00 4 400 78 b00 4 400 30 b00 4 400 30 b00 4 400
  //   30 b00 4 400 34 b00 4 400 a b00 4 400 43 b00 4 400 68 b00 4 400 65 b00 4 400 63 b00 4 400 6b b00 4
  //   400 20 b00 4 400 74 b00 4 400 68 b00 4 400 65 b00 4 400 20 b00 4 400 48 b00 4 400 65 b00 4 400 78
  //   b00 4 400 20 b00 4 400 4f b00 4 400 75 b00 4 400 74 b00 4 400 70 b00 4 400 75 b00 4 400 74 b00 4 400
  //   20 b00 4 400 a b00 4 400 50 b00 4 400 72 b00 4 400 65 b00 4 400 73 b00 4 400 73 b00 4 400 20 b00 4
  //   400 45 b00 4 400 6e b00 4 400 74 b00 4 400 65 b00 4 400 72 b00 4 400 20 b00 4 400 74 b00 4 400 6f
  //   b00 4 400 20 b00 4 400 43 b00 4 400 6f b00 4 400 6e b00 4 400 74 b00 4 400 69 b00 4 400 6e b00 4 400
  //   75 b00 4 400 65 b00 4 400 a b00 4 400 a 401 6 1000 0 1104 0 522 0 b08 2 1900 0 a00 1a0c 600 70e 400
  //   a b00 4 400 54 b00 4 400 65 b00 4 400 73 b00 4 400 74 b00 4 400 20 b00 4 400 33 b00 4 400 3a b00 4
  //   400 20 b00 4 400 53 b00 4 400 68 b00 4 400 69 b00 4 400 66 b00 4 400 74 b00 4 400 20 b00 4 400 4c
  //   b00 4 400 65 b00 4 400 66 b00 4 400 74 b00 4 400 20 b00 4 400 28 b00 4 400 31 b00 4 400 30 b00 4 400
  //   29 b00 4 400 a b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
endmodule

module Memory_Address_Register (
  input  CLK,
  input  RST,
  input  [15:0] Address_Bus,
  input  MI,
  output [15:0] MAR_Out
);

  Hex_Digit_Display hex_digit_display_1 (.value(MAR_Out[15:12]));  // open: dp
  Register #(.width(16)) register_1 (.D(Address_Bus), .en(MI), .clk(CLK), .Q(MAR_Out), .clr(RST));
  Hex_Digit_Display hex_digit_display_2 (.value(MAR_Out[11:8]));  // open: dp
  Hex_Digit_Display hex_digit_display_3 (.value(MAR_Out[7:4]));  // open: dp
  Hex_Digit_Display hex_digit_display_4 (.value(MAR_Out[3:0]));  // open: dp
endmodule

module InstructionRegister (
  input  CLK,
  input  RST,
  input  [15:0] DataIn,
  input  IIH,
  input  IOH,
  input  IOLA,
  input  IIL,
  input  IOL,
  output [15:0] IOH_Permanent,
  output [15:0] DataOut,
  output [15:0] IOL_Address
);

  wire [15:0] register_2_q;

  Register #(.width(16)) register_1 (.D(DataIn), .en(IIH), .clk(CLK), .Q(IOH_Permanent), .clr(RST));
  Register #(.width(16)) register_2 (.D(DataIn), .en(IIL), .clk(CLK), .Q(register_2_q), .clr(RST));
  assign DataOut = IOH ? IOH_Permanent : 16'bz;  // Controlled_Buffer controlled_buffer_1
  assign DataOut = IOL ? register_2_q : 16'bz;  // Controlled_Buffer controlled_buffer_2
  assign IOL_Address = IOLA ? register_2_q : 16'bz;  // Controlled_Buffer controlled_buffer_3
endmodule

module ALU (
  input  ALUResultOut,
  input  ALUAdd,
  input  ALUSub,
  input  ALUAND,
  input  ALUOR,
  input  ALUXOR,
  input  ALUSL,
  input  ALUSR,
  input  [15:0] Data_Bus,
  input  ALUOP1,
  input  CLK,
  input  RST,
  input  ALUOP2,
  output Overflow,
  output Zero,
  output [15:0] ALUOUT,
  output Carry,
  output Negative
);

  wire adder_1_cout, and_2_out, and_3_out, and_4_out, not_1_out, not_2_out, not_3_out, or_3_out, or_4_out,
       subtractor_1_bout;
  wire [14:0] controlled_buffer_1_out;
  wire [15:0] adder_1_out, and_1_out, or_1_out, register_1_q, register_2_q, shifter_1_out, shifter_2_out,
       subtractor_1_out, xor_1_out;

  Register #(.width(16)) register_1 (.D(Data_Bus), .en(ALUOP1), .clk(CLK), .Q(register_1_q), .clr(RST));
  Register #(.width(16)) register_2 (.D(Data_Bus), .en(ALUOP2), .clk(CLK), .Q(register_2_q), .clr(RST));
  not not_1 (not_1_out, register_2_q[15]);
  not not_2 (not_2_out, register_1_q[15]);
  Adder #(.width(16)) adder_1 (
    .a(register_1_q), .b(register_2_q), .out(adder_1_out), .cout(adder_1_cout));  // open: cin
  Subtractor #(.width(16)) subtractor_1 (
    .a(register_1_q), .b(register_2_q), .out(subtractor_1_out), .bout(subtractor_1_bout));  // open: bin
  assign and_1_out = register_1_q & register_2_q;  // AND_Gate and_1, 16 bits wide
  assign or_1_out = register_1_q | register_2_q;  // OR_Gate or_1, 16 bits wide
  assign xor_1_out = register_1_q ^ register_2_q;  // XOR_Gate xor_1, 16 bits wide
  Shifter #(.width(16)) shifter_1 (.in(register_1_q), .\dist (4'b0001), .out(shifter_1_out));
  Shifter #(.shift("lr"), .width(16)) shifter_2 (.in(register_1_q), .\dist (4'b0001), .out(shifter_2_out));
  and and_2 (and_2_out, not_1_out, not_2_out);
  assign {Negative, controlled_buffer_1_out} = ALUAdd ? adder_1_out : 16'bz;  // Controlled_Buffer controlled_buffer_1
  assign Carry = ALUAdd ? adder_1_cout : 1'bz;  // Controlled_Buffer controlled_buffer_2
  assign {Negative, controlled_buffer_1_out} = ALUSub ? subtractor_1_out : 16'bz;  // Controlled_Buffer controlled_buffer_3
  assign Carry = ALUSub ? subtractor_1_bout : 1'bz;  // Controlled_Buffer controlled_buffer_4
  assign {Negative, controlled_buffer_1_out} = ALUAND ? and_1_out : 16'bz;  // Controlled_Buffer controlled_buffer_5
  assign {Negative, controlled_buffer_1_out} = ALUOR ? or_1_out : 16'bz;  // Controlled_Buffer controlled_buffer_6
  assign {Negative, controlled_buffer_1_out} = ALUXOR ? xor_1_out : 16'bz;  // Controlled_Buffer controlled_buffer_7
  assign {Negative, controlled_buffer_1_out} = ALUSL ? shifter_1_out : 16'bz;  // Controlled_Buffer controlled_buffer_8
  assign {Negative, controlled_buffer_1_out} = ALUSR ? shifter_2_out : 16'bz;  // Controlled_Buffer controlled_buffer_9
  and and_3 (and_3_out, not_3_out, register_2_q[15], register_1_q[15]);
  and and_4 (and_4_out, and_2_out, Negative);
  not not_3 (not_3_out, Negative);
  Pull_Resistor pull_resistor_1 (.node(Carry));
  or or_2 (Overflow, and_3_out, and_4_out);
  Pull_Resistor pull_resistor_2 (.node({Negative, controlled_buffer_1_out}));
  Pull_Resistor pull_resistor_3 (.node(controlled_buffer_1_out[0]));
  or or_3 (or_3_out, controlled_buffer_1_out[0], controlled_buffer_1_out[1], controlled_buffer_1_out[2], controlled_buffer_1_out[3], controlled_buffer_1_out[4], controlled_buffer_1_out[5], controlled_buffer_1_out[6], controlled_buffer_1_out[7], controlled_buffer_1_out[8], controlled_buffer_1_out[9], controlled_buffer_1_out[10], controlled_buffer_1_out[11], controlled_buffer_1_out[12], controlled_buffer_1_out[13], controlled_buffer_1_out[14], Negative);
  or or_4 (or_4_out, ALUAdd, ALUSub);
  assign Zero = or_4_out ? ~or_3_out : 1'bz;  // Controlled_Inverter controlled_inverter_1
  Pull_Resistor pull_resistor_4 (.node(Zero));
  assign ALUOUT = ALUResultOut ? {Negative, controlled_buffer_1_out} : 16'bz;  // Controlled_Buffer controlled_buffer_10

  // Notes on the sheet:
  //   Zero: pull=up
  //   ADD
  //   Subtract
  //   AND
  //   OR
  //   XOR
  //   Logical Shift Left
  //   Logical Shift Right
endmodule

module FlagsRegister (
  input  FI,
  input  CLK,
  input  RST,
  input  Zero_Flag_In,
  input  Carry_Flag_In,
  input  Input_Ready_Flag_In,
  input  Negative_Flag_In,
  input  Overflow_Flag_In,
  input  [15:0] Data_Bus,
  input  FSI,
  output [7:0] Flags_Out
);

  wire FW;
  wire [15:0] controlled_buffer_3_out;

  assign controlled_buffer_3_out[1] = FI ? Carry_Flag_In : 1'bz;  // Controlled_Buffer controlled_buffer_1
  assign controlled_buffer_3_out[2] = FI ? Input_Ready_Flag_In : 1'bz;  // Controlled_Buffer controlled_buffer_2
  assign controlled_buffer_3_out = FSI ? Data_Bus : 16'bz;  // Controlled_Buffer controlled_buffer_3
  assign controlled_buffer_3_out[3] = FI ? Negative_Flag_In : 1'bz;  // Controlled_Buffer controlled_buffer_4
  assign controlled_buffer_3_out[4] = FI ? Overflow_Flag_In : 1'bz;  // Controlled_Buffer controlled_buffer_5
  assign controlled_buffer_3_out[0] = FI ? Zero_Flag_In : 1'bz;  // Controlled_Buffer controlled_buffer_6
  Pull_Resistor pull_resistor_1 (.node(controlled_buffer_3_out[0]));
  Pull_Resistor pull_resistor_2 (.node(controlled_buffer_3_out[1]));
  Pull_Resistor pull_resistor_3 (.node(controlled_buffer_3_out[2]));
  Pull_Resistor pull_resistor_4 (.node(controlled_buffer_3_out[3]));
  Pull_Resistor pull_resistor_5 (.node(controlled_buffer_3_out[4]));
  or or_1 (FW, FSI, FI);
  Register #(.width(1)) register_1 (.D(controlled_buffer_3_out[0]), .en(FW), .clk(CLK), .Q(Flags_Out[0]), .clr(RST));
  Register #(.width(1)) register_2 (.D(controlled_buffer_3_out[1]), .en(FW), .clk(CLK), .Q(Flags_Out[1]), .clr(RST));
  Register #(.width(1)) register_3 (.D(controlled_buffer_3_out[2]), .en(FW), .clk(CLK), .Q(Flags_Out[2]), .clr(RST));
  Register #(.width(1)) register_4 (.D(controlled_buffer_3_out[3]), .en(FW), .clk(CLK), .Q(Flags_Out[3]), .clr(RST));
  Register #(.width(1)) register_5 (.D(controlled_buffer_3_out[4]), .en(FW), .clk(CLK), .Q(Flags_Out[4]), .clr(RST));
endmodule

module Control_Logic (
  input  CLK,
  input  [15:0] Instruction,
  output AO,
  output BO,
  output XO,
  output YO,
  output AI,
  output BI,
  output XI,
  output YI,
  output [3:0] ALUOP,
  output CE,
  output CO,
  output MI,
  output RAO,
  output RAI,
  output ROO,
  output NC,
  output HLT,
  output RegOut,
  output RegIn,
  output IIL,
  output IIH,
  output IOL,
  output IOH,
  output IOO,
  output IOI,
  output JMP,
  output JC,
  output JZ,
  output JNZ,
  output ALURO,
  output EndCMD,
  output IOLA,
  output FI,
  output ALUOP1,
  output ALUOP2,
  output JNI,
  output SPIn,
  output SPDOut,
  output SPAOut,
  output SPINC,
  output SPDEC,
  output JN,
  output JO,
  output FO,
  output FSI,
  output INTC,
  output JMPI,
  output BSRO,
  output BSRA
);

  wire demultiplexer_3_out0, demultiplexer_3_out1, demultiplexer_3_out2, demultiplexer_3_out3,
       demultiplexer_3_out4, demultiplexer_3_out5, demultiplexer_3_out6, demultiplexer_3_out7,
       demultiplexer_3_out8, demultiplexer_3_out9, demultiplexer_3_out10, demultiplexer_3_out11,
       demultiplexer_3_out12, demultiplexer_3_out13, demultiplexer_3_out14, demultiplexer_3_out15, or_1_out,
       RST;
  wire [2:0] pull_resistor_3_node;
  wire [3:0] counter_1_q;

  Demultiplexer #(.select(2)) demultiplexer_1 (
    .out0(AO), .out1(BO), .out2(XO), .out3(YO), .in(RegOut), .sel(Instruction[3:2]));
  Demultiplexer #(.select(2)) demultiplexer_2 (
    .out0(AI), .out1(BI), .out2(XI), .out3(YI), .in(RegIn), .sel(Instruction[1:0]));
  Pull_Resistor pull_resistor_1 (.node(pull_resistor_3_node[2]));
  Pull_Resistor pull_resistor_2 (.node(pull_resistor_3_node[1]));
  Pull_Resistor pull_resistor_3 (.node(pull_resistor_3_node[0]));
  or or_1 (or_1_out, RST, EndCMD);
  Counter #(.max('hf), .width(4)) counter_1 (
    .clr(or_1_out), .up(1'b1), .count(1'b1), .clk(CLK), .Q(counter_1_q));  // open: load, D, carry
  ROM #(.addrWidth(15)) rom_1 (
    .addr({pull_resistor_3_node, Instruction[15:8], counter_1_q}), .data({HLT, NC, ROO, RAI, RAO, MI, CO, CE}));
  ROM #(.addrWidth(15)) rom_2 (
    .addr({pull_resistor_3_node, Instruction[15:8], counter_1_q}),
    .data({IOI, IOO, IOH, IOL, IIH, IIL, RegIn, RegOut}));
  ROM #(.addrWidth(15)) rom_3 (
    .addr({pull_resistor_3_node, Instruction[15:8], counter_1_q}),
    .data({FI, IOLA, EndCMD, ALURO, JNZ, JZ, JC, JMP}));
  ROM #(.addrWidth(15)) rom_4 (
    .addr({pull_resistor_3_node, Instruction[15:8], counter_1_q}),
    .data({SPDEC, SPINC, SPAOut, SPDOut, SPIn, JNI, ALUOP2, ALUOP1}));
  ROM #(.addrWidth(15)) rom_5 (
    .addr({pull_resistor_3_node, Instruction[15:8], counter_1_q}),
    .data({BSRA, BSRO, JMPI, INTC, FSI, FO, JO, JN}));
  Demultiplexer #(.select(4)) demultiplexer_3 (
    .out0(demultiplexer_3_out0), .out1(demultiplexer_3_out1), .out2(demultiplexer_3_out2),
    .out3(demultiplexer_3_out3), .out4(demultiplexer_3_out4), .out5(demultiplexer_3_out5),
    .out6(demultiplexer_3_out6), .out7(demultiplexer_3_out7), .out8(demultiplexer_3_out8),
    .out9(demultiplexer_3_out9), .out10(demultiplexer_3_out10), .out11(demultiplexer_3_out11),
    .out12(demultiplexer_3_out12), .out13(demultiplexer_3_out13), .out14(demultiplexer_3_out14),
    .out15(demultiplexer_3_out15), .in(1'b1), .sel(counter_1_q));
  LED led_1 (.in(demultiplexer_3_out0));
  LED led_2 (.in(demultiplexer_3_out1));
  LED led_3 (.in(demultiplexer_3_out2));
  LED led_4 (.in(demultiplexer_3_out3));
  LED led_5 (.in(demultiplexer_3_out4));
  LED led_6 (.in(demultiplexer_3_out5));
  LED led_7 (.in(demultiplexer_3_out6));
  LED led_8 (.in(demultiplexer_3_out7));
  LED led_9 (.in(demultiplexer_3_out8));
  LED led_10 (.in(demultiplexer_3_out9));
  LED led_11 (.in(demultiplexer_3_out10));
  LED led_12 (.in(demultiplexer_3_out11));
  LED led_13 (.in(demultiplexer_3_out12));
  LED led_14 (.in(demultiplexer_3_out13));
  LED led_15 (.in(demultiplexer_3_out14));
  LED led_16 (.in(demultiplexer_3_out15));

  assign ALUOP = Instruction[7:4];

  // Notes on the sheet:
  //   Source Register
  //   Destination Register
  //   contents of rom_1 (hex, n*v repeats v):
  //   0 6 21 14*0 6 21 14*0 6 21 6 21 4 8 10*0 6 21 6 21 4 10 10*0 6 21 6 21 12*0 6 21 14*0 6 21 6 21 12*0
  //   6 21 6 21 12*0 6 21 6 21 12*0 6 21 6 21 12*0 6 21 6 21 12*0 6 21 6 21 44*0 6 21 6 21 12*0 6 21 80
  //   13*0 6 21 14*0 6 21 14*0 6 21 14*0 6 21 14*0 6 21 14*0 6 21 0 4 8 11*0 6 21 4 10 12*0 6 21 14*0 6 21
  //   14*0 6 21 30*0 6 21 14*0 6 21 6 21 12*0 6 21 6 21 12*0 6 21 4 10 12*0 6 21 0 4 8 11*0 6 21 6 21 12*0
  //   6 21 6 21 12*0 6 21 6 21
  //   contents of rom_2 (hex, n*v repeats v):
  //   0 0 8 15*0 8 3 14*0 8 0 4 0 2 11*0 8 0 4 0 1 11*0 8 0 4 12 12*0 8 2 14*0 8 0 4 10 12*0 8 0 4 10 12*0
  //   8 0 4 10 12*0 8 0 4 10 12*0 8 0 4 10 12*0 8 0 4 41 44*0 8 0 4 82 12*0 8 15*0 8 1 14*0 8 1 14*0 8
  //   15*0 8 1 14*0 8 2 14*0 8 0 0 2 12*0 8 0 1 13*0 8 15*0 8 15*0 8 31*0 8 5 10 13*0 8 0 4 10 12*0 8 0 4
  //   10 12*0 8 15*0 8 15*0 8 0 4 13*0 8 0 4 10 12*0 8 0 4 10
  //   contents of rom_3 (hex, n*v repeats v):
  //   0 0 0 20 16*0 20 16*0 40 0 20 13*0 40 0 20 14*0 20 12*0 10 80 20 15*0 1 20 14*0 4 20 14*0 8 20 14*0
  //   2 20 15*0 20 14*0 40 20 46*0 40 80 20 28*0 20 15*0 20 14*0 80 20 15*0 20 15*0 20 17*0 20 15*0 20
  //   13*0 20 15*0 20 14*0 80 20 31*0 1 20 16*0 20 15*0 20 15*0 20 15*0 20 15*0 20 15*0 20 15*0 20
  //   contents of rom_4 (hex, n*v repeats v):
  //   165*0 4 93*0 1 15*0 2 31*0 8 15*0 10 15*0 40 20 14*0 20 0 80 13*0 40 15*0 80 95*0 20 0 80 13*0 40 20
  //   contents of rom_5 (hex, n*v repeats v):
  //   10 15*0 10 15*0 10 15*0 10 15*0 10 15*0 10 15*0 10 15*0 10 15*0 10 15*0 10 15*0 10 15*0 10 47*0 10
  //   15*0 10 15*0 10 15*0 10 15*0 10 15*0 10 15*0 10 15*0 10 15*0 10 15*0 10 15*0 10 15*0 10 31*0 10 15*0
  //   10 4*0 1 10*0 10 4*0 2 10*0 10 0 0 0 4 11*0 10 4*0 8 10*0 10 4*0 20 10*0 10 4*0 40 10*0 10 4*0 80
endmodule

module Output_Display (
  input  [15:0] Address_Bus,
  input  IOO,
  input  [15:0] Data_Bus,
  input  CLK,
  input  RST
);

  wire and_1_out, nor_1_out;
  wire [15:0] register_1_q;

  nor nor_1 (nor_1_out, Address_Bus[2], Address_Bus[3], Address_Bus[4], Address_Bus[5], Address_Bus[6], Address_Bus[7], Address_Bus[8], Address_Bus[9], Address_Bus[10], Address_Bus[11], Address_Bus[12], Address_Bus[13], Address_Bus[14], Address_Bus[15], Address_Bus[0]);
  and and_1 (and_1_out, Address_Bus[1], nor_1_out, IOO);
  Register #(.width(16)) register_1 (.D(Data_Bus), .en(and_1_out), .clk(CLK), .Q(register_1_q), .clr(RST));
  Pull_Resistor pull_resistor_1 (.node(register_1_q));
  Hex_Digit_Display hex_digit_display_1 (.value(register_1_q[15:12]));  // open: dp
  Hex_Digit_Display hex_digit_display_2 (.value(register_1_q[11:8]));  // open: dp
  Hex_Digit_Display hex_digit_display_3 (.value(register_1_q[7:4]));  // open: dp
  Hex_Digit_Display hex_digit_display_4 (.value(register_1_q[3:0]));  // open: dp
endmodule

module DisplayTTY (
  input  [15:0] Data_Bus,
  input  CLK,
  input  IOO,
  input  [15:0] Address_Bus
);

  wire and_1_out, and_2_out, nor_1_out;

  nor nor_1 (nor_1_out, Address_Bus[0], Address_Bus[1], Address_Bus[3], Address_Bus[4], Address_Bus[5], Address_Bus[6], Address_Bus[7], Address_Bus[8], Address_Bus[9], Address_Bus[10], Address_Bus[11], Address_Bus[12], Address_Bus[13], Address_Bus[14], Address_Bus[15]);
  and and_1 (and_1_out, IOO, Address_Bus[2], nor_1_out);
  TTY #(.rows(16)) tty_1 (.data(Data_Bus[6:0]), .clk(CLK), .we(and_1_out), .clr(and_2_out));
  and and_2 (and_2_out, and_1_out, Data_Bus[7]);
endmodule

module Stack_Pointer (
  input  SPINC,
  input  SPDEC,
  input  [15:0] Data_Bus_In,
  input  SPIn,
  input  SPAOut,
  input  CLK,
  input  RST,
  input  SPDOut,
  output [15:0] Address_Bus_Out,
  output [15:0] Data_Bus_Out
);

  wire or_1_out, or_2_out;
  wire [15:0] adder_1_out, controlled_buffer_1_out, register_1_q, subtractor_1_out;

  or or_1 (or_1_out, CLK, SPDEC, SPINC);
  assign controlled_buffer_1_out = SPIn ? Data_Bus_In : 16'bz;  // Controlled_Buffer controlled_buffer_1
  or or_2 (or_2_out, SPIn, SPDEC, SPINC);
  assign controlled_buffer_1_out = SPINC ? adder_1_out : 16'bz;  // Controlled_Buffer controlled_buffer_2
  Adder #(.width(16)) adder_1 (.a(register_1_q), .b(16'h1), .out(adder_1_out));  // open: cin, cout
  assign controlled_buffer_1_out = SPDEC ? subtractor_1_out : 16'bz;  // Controlled_Buffer controlled_buffer_3
  Subtractor #(.width(16)) subtractor_1 (.a(register_1_q), .b(16'h1), .out(subtractor_1_out));  // open: bin, bout
  Register #(.width(16)) register_1 (
    .D(controlled_buffer_1_out), .en(or_2_out), .clk(or_1_out), .Q(register_1_q), .clr(RST));
  assign Address_Bus_Out = SPAOut ? register_1_q : 16'bz;  // Controlled_Buffer controlled_buffer_4
  assign Data_Bus_Out = SPDOut ? register_1_q : 16'bz;  // Controlled_Buffer controlled_buffer_5
endmodule

module Interupt_Control (
  input  INT_Trig,
  input  CLK,
  input  RST,
  input  INT_RET,
  input  INTC,
  input  [15:0] PCAO,
  output INTJMP,
  output [15:0] Data_Bus
);

  wire and_1_out, j_k_ff_1_q;
  wire [15:0] register_1_q;
  wire [15:8] pull_resistor_2_node;

  or or_1 (INTJMP, and_1_out, INT_RET);
  and and_1 (and_1_out, j_k_ff_1_q, INTC);
  Pull_Resistor pull_resistor_1 (.node(INTC));
  assign Data_Bus = INTC ? {{7{pull_resistor_2_node[15]}}, {9{pull_resistor_2_node[8]}}} : 16'bz;  // Controlled_Buffer controlled_buffer_1
  assign Data_Bus = INT_RET ? register_1_q : 16'bz;  // Controlled_Buffer controlled_buffer_2
  Register #(.width(16)) register_1 (.D(PCAO), .en(INT_Trig), .clk(CLK), .Q(register_1_q), .clr(RST));
  Pull_Resistor pull_resistor_2 (.node(pull_resistor_2_node[8]));
  Pull_Resistor #(.pull(1)) pull_resistor_3 (.node(pull_resistor_2_node[15]));
  J_K_Flip_Flop j_k_ff_1 (.J(INT_Trig), .K(and_1_out), .clk(CLK), .Q(j_k_ff_1_q), .reset(RST));  // open: Qn, preset

  // Notes on the sheet:
  //   Data_Bus: pull=down
endmodule

module Bank_Switcher (
  input  BSRO,
  input  BSRA,
  input  CLK,
  input  RST,
  output ROM_Active,
  output RAM_Active
);

  wire controlled_buffer_1_out, or_1_out;

  assign controlled_buffer_1_out = BSRO ? 1'b0 : 1'bz;  // Controlled_Buffer controlled_buffer_1
  assign controlled_buffer_1_out = BSRA ? 1'b1 : 1'bz;  // Controlled_Buffer controlled_buffer_2
  or or_1 (or_1_out, BSRO, BSRA);
  Register #(.width(1)) register_1 (.D(controlled_buffer_1_out), .en(or_1_out), .clk(CLK), .Q(RAM_Active), .clr(RST));
  Pull_Resistor pull_resistor_1 (.node(controlled_buffer_1_out));
  not not_1 (ROM_Active, RAM_Active);
endmodule
